# Fritzing sketch IoT en 90 minutos (saved by Fritzing 0.9.3b)
breadboards: 1

parts:
  WeMos_D1_Mini1 = WeMos D1 Mini
  DHT1 = DHT11 Humitidy and Temperature Sensor
  R2 = Resistor [tolerance=±5% resistance=220 package=THT]
  LED1 = LED - 5mm [color="Red (633nm)" package="5 mm [THT]"]
  S1 = Pushbutton [package="[THT]"]
  R3 = Resistor [tolerance=±5% resistance=10k package=THT]

nets:
  3V3: WeMos_D1_Mini1.3V3, DHT1.VDD, R3.Pin_0
  N1: WeMos_D1_Mini1.D2, DHT1.DATA, R3.Pin_1
  N2: WeMos_D1_Mini1.D3, S1.Pin_1, S1.Pin_2
  N3: WeMos_D1_Mini1.D4, LED1.anode
  N4: WeMos_D1_Mini1.G, DHT1.GND, R2.Pin_0, S1.Pin_3, S1.Pin_4
  N5: R2.Pin_1, LED1.cathode

custom parts:
  DHT11 Humitidy and Temperature Sensor: DHT11 Humidity and Temperature Sensor
